// Logisim project cpu.circ as structural Verilog: 1 circuit, main circuit main
module main (
);

  wire ACC_WE, adder_1_cout, AH_OE, AL_OE, and_1_out, and_2_out, and_3_out, and_4_out, and_5_out, and_6_out,
       and_7_out, and_8_out, and_9_out, and_11_out, and_13_out, and_14_out, BP_CNT, BP_DIR, BP_H_WE,
       BP_L_carry, BP_L_WE, BP_OE, button_1_out, button_2_out, CARRY, CLK, clock_1_out, d_ff_1_q, END_INSTR,
       EQUAL, HALT, IR_WE, JMP_ENABLE, LESS, MORE, nand_2_out, not_1_out, not_2_out, not_3_out, not_4_out,
       or_2_out, PC_CNT, PC_H_WE, PC_L_carry, PC_L_WE, PC_OE, RAM_OE, RAM_WE, RES_OE, RES_WE, RST, SP_CNT,
       SP_H_WE, SP_L_carry, SP_L_WE, SP_OE, subtractor_1_bout;
  wire [2:0] ALU_SEL;
  wire [3:0] counter_1_q, multiplexer_2_out;
  wire [6:0] keyboard_1_data;
  wire [7:0] ACC_q, adder_1_out, and_12_out, BP_H_q, BP_L_q, controlled_buffer_1_out,
       controlled_buffer_1_out_2, controlled_buffer_4_out, multiplexer_1_out, nand_1_out, or_1_out, PC_H_q,
       PC_L_q, register_1_q, RES_q, shifter_1_out, SP_H_q, SP_L_q, subtractor_1_out, xor_1_out;
  wire [10:0] rom_1_data;

  and and_1 (and_1_out, PC_L_WE, JMP_ENABLE);
  and and_2 (and_2_out, PC_H_WE, JMP_ENABLE);
  Counter PC_L (
    .load(and_1_out), .D(controlled_buffer_4_out), .count(PC_CNT), .Q(PC_L_q), .carry(PC_L_carry), .clk(CLK),
    .clr(RST));  // open: up
  Counter PC_H (
    .load(and_2_out), .D(controlled_buffer_4_out), .count(and_3_out), .Q(PC_H_q), .clk(CLK), .clr(RST));  // open: carry, up
  Counter SP_L (
    .load(SP_L_WE), .D(controlled_buffer_4_out), .count(SP_CNT), .Q(SP_L_q), .carry(SP_L_carry), .up(BP_DIR),
    .clk(CLK), .clr(RST));
  Counter SP_H (
    .load(SP_H_WE), .D(controlled_buffer_4_out), .count(and_4_out), .Q(SP_H_q), .up(BP_DIR), .clk(CLK),
    .clr(RST));  // open: carry
  Counter BP_L (
    .load(BP_L_WE), .D(controlled_buffer_4_out), .count(BP_CNT), .Q(BP_L_q), .carry(BP_L_carry), .up(BP_DIR),
    .clk(CLK), .clr(RST));
  Counter BP_H (
    .load(BP_H_WE), .D(controlled_buffer_4_out), .count(and_5_out), .Q(BP_H_q), .up(BP_DIR), .clk(CLK),
    .clr(RST));  // open: carry
  and and_3 (and_3_out, PC_L_carry, PC_CNT);
  and and_4 (and_4_out, SP_L_carry, SP_CNT);
  and and_5 (and_5_out, BP_L_carry, BP_CNT);
  assign {controlled_buffer_1_out_2, controlled_buffer_1_out} = PC_OE ? {PC_H_q, PC_L_q} : 16'bz;  // Controlled_Buffer controlled_buffer_1
  assign {controlled_buffer_1_out_2, controlled_buffer_1_out} = SP_OE ? {SP_H_q, SP_L_q} : 16'bz;  // Controlled_Buffer controlled_buffer_2
  assign {controlled_buffer_1_out_2, controlled_buffer_1_out} = BP_OE ? {BP_H_q, BP_L_q} : 16'bz;  // Controlled_Buffer controlled_buffer_3
  assign controlled_buffer_4_out = AL_OE ? controlled_buffer_1_out : 8'bz;  // Controlled_Buffer controlled_buffer_4
  assign controlled_buffer_4_out = AH_OE ? controlled_buffer_1_out_2 : 8'bz;  // Controlled_Buffer controlled_buffer_5
  // Probe on {controlled_buffer_1_out_2, controlled_buffer_1_out}
  Button button_1 (.out(button_1_out));
  D_Flip_Flop d_ff_1 (.D(1'b0), .clk(HALT), .Q(d_ff_1_q), .preset(button_1_out), .reset(button_2_out));  // open: Qn
  Button button_2 (.out(button_2_out));
  Button button_3 (.out(RST));
  RAM #(.addrWidth(15), .asyncread("true"), .databus("bidir")) ram_1 (
    .addr({controlled_buffer_1_out_2[6:0], controlled_buffer_1_out}), .we(and_6_out), .oe(and_7_out),
    .clk(CLK), .data(controlled_buffer_4_out));
  and and_6 (and_6_out, ~controlled_buffer_1_out_2[7], RAM_WE);  // AND_Gate
  and and_7 (and_7_out, ~controlled_buffer_1_out_2[7], RAM_OE);  // AND_Gate
  TTY tty_1 (.data(controlled_buffer_4_out[6:0]), .clk(CLK), .we(and_8_out), .clr(RST));
  and and_8 (and_8_out, controlled_buffer_1_out_2[7], RAM_WE);
  and and_9 (and_9_out, controlled_buffer_1_out_2[7], RAM_OE);
  Clock clock_1 (.out(clock_1_out));
  Keyboard keyboard_1 (.clk(CLK), .re(and_9_out), .clr(RST), .data(keyboard_1_data));  // open: avail
  and and_10 (CLK, d_ff_1_q, clock_1_out);
  assign controlled_buffer_4_out = and_9_out ? {1'b0, keyboard_1_data} : 8'bz;  // Controlled_Buffer controlled_buffer_6
  Pull_Resistor pull_resistor_1 (.node(controlled_buffer_4_out));
  Register ACC (.D(controlled_buffer_4_out), .en(ACC_WE), .clk(CLK), .Q(ACC_q), .clr(RST));
  // Probe on controlled_buffer_4_out
  Register register_1 (.D(controlled_buffer_4_out), .en(IR_WE), .clk(CLK), .Q(register_1_q), .clr(RST));
  assign controlled_buffer_4_out = RES_OE ? RES_q : 8'bz;  // Controlled_Buffer controlled_buffer_7
  not not_1 (not_1_out, CLK);
  and and_11 (and_11_out, not_1_out, CLK);
  Adder adder_1 (.a(controlled_buffer_4_out), .b(ACC_q), .out(adder_1_out), .cin(CARRY), .cout(adder_1_cout));
  Subtractor subtractor_1 (
    .a(controlled_buffer_4_out), .b(ACC_q), .out(subtractor_1_out), .bin(CARRY), .bout(subtractor_1_bout));
  assign and_12_out = controlled_buffer_4_out & ACC_q;  // AND_Gate and_12, 8 bits wide
  assign or_1_out = controlled_buffer_4_out | ACC_q;  // OR_Gate or_1, 8 bits wide
  assign nand_1_out = ~(controlled_buffer_4_out & ACC_q);  // NAND_Gate nand_1, 8 bits wide
  assign xor_1_out = controlled_buffer_4_out ^ ACC_q;  // XOR_Gate xor_1, 8 bits wide
  Shifter #(.shift("lr")) shifter_1 (.in(controlled_buffer_4_out), .\dist (ACC_q[2:0]), .out(shifter_1_out));
  Comparator comparator_1 (
    .a(controlled_buffer_4_out), .b(ACC_q), .gt(multiplexer_2_out[1]), .eq(multiplexer_2_out[2]),
    .lt(multiplexer_2_out[3]));
  Counter #(.max('hf), .width(4)) counter_1 (
    .count(1'b1), .Q(counter_1_q), .clk(CLK), .clr(or_2_out));  // open: load, D, carry, up
  or or_2 (or_2_out, and_13_out, RST);
  and and_13 (and_13_out, and_11_out, END_INSTR);
  ROM #(.addrWidth(12), .dataWidth(16)) rom_1 (
    .addr({register_1_q, counter_1_q}),
    .data({END_INSTR, HALT, ALU_SEL, rom_1_data[10:4], BP_DIR, rom_1_data[2:0]}));
  Multiplexer #(.select(3), .width(8)) multiplexer_1 (
    .in0(adder_1_out), .in1(subtractor_1_out), .in2(and_12_out), .in3(or_1_out), .in4(nand_1_out),
    .in5(xor_1_out), .in6(shifter_1_out), .in7(controlled_buffer_4_out), .out(multiplexer_1_out),
    .sel(ALU_SEL));
  // Probe on ALU_SEL
  Multiplexer #(.select(3)) multiplexer_2 (
    .in0(adder_1_cout), .in1(subtractor_1_bout), .in2(1'b0), .in3(1'b0), .in4(1'b0), .in5(1'b0), .in6(1'b0),
    .in7(1'b0), .out(multiplexer_2_out[0]), .sel(ALU_SEL));
  nand nand_2 (nand_2_out, ALU_SEL[0], ALU_SEL[1], ALU_SEL[2]);
  and and_14 (and_14_out, nand_2_out, RES_WE);
  Register RES (.D(multiplexer_1_out), .en(RES_WE), .clk(CLK), .Q(RES_q), .clr(RST));
  // Probe on multiplexer_1_out
  Register #(.width(4)) register_2 (
    .D(multiplexer_2_out), .en(and_14_out), .clk(CLK), .Q({LESS, EQUAL, MORE, CARRY}), .clr(RST));
  Decoder #(.enable("false"), .select(2)) decoder_1 (
    .out0(PC_OE), .out1(SP_OE), .out2(BP_OE), .sel(rom_1_data[1:0]));  // open: out3
  Decoder #(.select(2)) decoder_2 (
    .out0(PC_CNT), .out1(SP_CNT), .out2(BP_CNT), .sel(rom_1_data[1:0]), .en(rom_1_data[2]));  // open: out3
  not not_2 (not_2_out, rom_1_data[7]);
  Decoder #(.select(3)) decoder_3 (
    .out0(IR_WE), .out1(RAM_WE), .out2(ACC_WE), .out3(RES_WE), .out4(PC_L_WE), .out5(PC_H_WE),
    .out6(SP_L_WE), .out7(SP_H_WE), .sel(rom_1_data[6:4]), .en(not_2_out));
  Decoder #(.select(3)) decoder_4 (
    .out0(BP_L_WE), .out1(BP_H_WE), .sel(rom_1_data[6:4]), .en(rom_1_data[7]));  // open: out2, out3, out4, out5, out6, out7
  Decoder #(.enable("false"), .select(3)) decoder_5 (
    .out0(RAM_OE), .out1(RES_OE), .out2(AL_OE), .out3(AH_OE), .sel(rom_1_data[10:8]));  // open: out4, out5, out6, out7
  not not_3 (not_3_out, CARRY);
  not not_4 (not_4_out, EQUAL);
  // Probe on ALU_SEL
  Multiplexer #(.select(3)) multiplexer_3 (
    .in0(1'b1), .in1(CARRY), .in2(not_3_out), .in3(MORE), .in4(LESS), .in5(EQUAL), .in6(not_4_out),
    .in7(1'b1), .out(JMP_ENABLE), .sel(ALU_SEL));

  // Other names for the same wires on the sheet: SP_DIR = BP_DIR

  // Notes on the sheet:
  //   contents of rom_1 (hex, n*v repeats v):
  //   3804 8000 14*0 3804 3874 b864 13*0 3804 3894 b884 13*0 3804 3834 38f5 b911 12*0 3804 382d 31 b911
  //   12*0 3804 382d 831 b911 12*0 3804 382d 2031 b911 12*0 3804 3832 38f5 b911 12*0 3804 383d b912 13*0
  //   3804 3a32 38f5 3911 3b32 38f5 b911 9*0 3804 389d b88d 13*0 3804 3b91 ba81 13*0 3804 3b72 ba62 13*0
  //   3804 3834 44 8150 12*0 3804 3a30 38f5 3911 3b30 38f5 3911 3834 44 8150 6*0 3804 385d 384d 38f4 b8f4
  //   11*0 3804 3820 232 3980 3f20 332 3990 3832 38f5 3911 3824 a32 3980 3f20 b32 b990 3804 3820 a32 3980
  //   3f20 b32 3990 3832 38f5 3911 3824 232 3980 3f20 332 b990 3804 3820 232 3980 3f20 332 3990 383d 3912
  //   3824 a32 3980 3f20 b32 b990 0 3804 3820 a32 3980 3f20 b32 3990 383d 3912 3824 232 3980 3f20 332 b990
  //   0 3804 b8fd 14*0 3804 382d 3031 b911 12*0 3804 c000 14*0 3804 b8fe 14*0 3804 b8f6 14*0 3804 382d
  //   8031 109*0 3804 3834 2044 a150 12*0 3804 3834 1844 9950 12*0 3804 3834 2844 a950 12*0 3804 3834 3044
  //   b150 12*0 3804 3834 844 8950 12*0 3804 3834 1044 9150
  //   ADDRESS COUNT
  //   DATA SOURCE
  //   ALU CONTROL
  //   ADDRESS SOURCE
  //   DATA DESTINATION
endmodule
